// Logisim project 15-02.circ as structural Verilog: 5 circuits, main circuit main
module main (
  input  [3:0] A,
  input  [3:0] B,
  output Overflow,
  output Overflow_2,
  output [3:0] S,
  output [3:0] S_2
);

  ADD_4 add_4_1 (.in_1(A), .in_2(B), .out_4(Overflow), .in_3(1'b0), .out_5(S));
  SUB_4 sub_4_1 (.in_2(A), .out_4(Overflow_2), .in_1(B), .in_3(1'b0), .out_5(S_2));
endmodule

module ADD_1 (
  input  A,
  input  B,
  input  VEM_1,
  output S,
  output VAL_1
);

  wire and_1_out, and_2_out, or_1_out, xor_1_out;

  xor xor_1 (xor_1_out, A, B);
  or or_1 (or_1_out, B, VEM_1);
  and and_1 (and_1_out, or_1_out, A);
  and and_2 (and_2_out, B, VEM_1);
  xor xor_2 (S, xor_1_out, VEM_1);
  or or_2 (VAL_1, and_1_out, and_2_out);
endmodule

module SUB_1 (
  input  A,
  input  B,
  input  VEM_1,
  output S,
  output VAI_1
);

  wire and_1_out, and_2_out, not_1_out, or_1_out, xor_1_out;

  not not_1 (not_1_out, A);
  xor xor_1 (xor_1_out, A, B);
  or or_1 (or_1_out, VEM_1, B);
  and and_1 (and_1_out, or_1_out, not_1_out);
  and and_2 (and_2_out, B, VEM_1);
  xor xor_2 (S, xor_1_out, VEM_1);
  or or_2 (VAI_1, and_1_out, and_2_out);
endmodule

module ADD_4 (
  input  [3:0] in_1,
  input  [3:0] in_2,
  input  in_3,
  output out_4,
  output [3:0] out_5
);

  wire add_1_2_val_1, add_1_3_val_1, add_1_4_val_1;

  ADD_1 add_1_1 (.A(in_1[3]), .B(in_2[3]), .VEM_1(add_1_2_val_1), .S(out_5[3]), .VAL_1(out_4));
  ADD_1 add_1_2 (.A(in_1[2]), .B(in_2[2]), .VEM_1(add_1_3_val_1), .S(out_5[2]), .VAL_1(add_1_2_val_1));
  ADD_1 add_1_3 (.A(in_1[1]), .B(in_2[1]), .VEM_1(add_1_4_val_1), .S(out_5[1]), .VAL_1(add_1_3_val_1));
  ADD_1 add_1_4 (.A(in_1[0]), .B(in_2[0]), .VEM_1(in_3), .S(out_5[0]), .VAL_1(add_1_4_val_1));

  // Notes on the sheet:
  //   ADD_1
  //   ADD_1
  //   ADD_1
endmodule

module SUB_4 (
  input  [3:0] in_1,
  input  [3:0] in_2,
  input  in_3,
  output out_4,
  output [3:0] out_5
);

  wire sub_1_2_s, sub_1_3_s, sub_1_4_s;

  SUB_1 sub_1_1 (.A(in_2[3]), .B(in_1[3]), .VEM_1(sub_1_2_s), .S(out_4), .VAI_1(out_5[3]));
  SUB_1 sub_1_2 (.A(in_2[2]), .B(in_1[2]), .VEM_1(sub_1_3_s), .S(sub_1_2_s), .VAI_1(out_5[2]));
  SUB_1 sub_1_3 (.A(in_2[1]), .B(in_1[1]), .VEM_1(sub_1_4_s), .S(sub_1_3_s), .VAI_1(out_5[1]));
  SUB_1 sub_1_4 (.A(in_2[0]), .B(in_1[0]), .VEM_1(in_3), .S(sub_1_4_s), .VAI_1(out_5[0]));
endmodule
