// Logisim project PedroHenriqueNovelliSoares.circ as structural Verilog: 16 circuits, main circuit main
module main (
);

  wire clock_1_out, d_ff_1_q, d_ff_2_q, not_1_out, not_2_out, Reset_out, uc_1_clk_ac, uc_1_clk_pc,
       uc_1_clk_ram, uc_1_clk_ri, \uc_1_direção , uc_1_e, uc_1_load, uc_1_r_w, uc_1_rst_pc, ula_1_overflow,
       ula_1_zero;
  wire [2:0] \uc_1_operação ;
  wire [3:0] counter_1_q, flipflop_1_q, mux_1_out_4, ram_1_data, \uc_1_b_endereço , uc_1_dados,
       uc_1_operando, ula_1_s;
  wire [7:0] ir_1_q, rom_1_data;

  Counter #(.width(4), .max('hf), .trigger("falling")) counter_1 (
    .load(uc_1_load), .D(uc_1_dados), .count(not_1_out), .Q(counter_1_q), .clk(uc_1_clk_pc), .clr(uc_1_rst_pc));  // open: carry
  not not_1 (not_1_out, uc_1_load);
  UC uc_1 (
    .Operando(uc_1_operando), .\Direção (\uc_1_direção ), .E(uc_1_e), .\Operação (\uc_1_operação ),
    .\Instrução (ir_1_q), .\B_ENDEREÇO (\uc_1_b_endereço ), .Clock(clock_1_out), .Rst_PC(uc_1_rst_pc),
    .Reset(Reset_out), .clk_RI(uc_1_clk_ri), .clk_PC(uc_1_clk_pc), .clk_AC(uc_1_clk_ac),
    .clk_RAM(uc_1_clk_ram), .Dados(uc_1_dados), .Zero(d_ff_2_q), .Overflow(d_ff_1_q), .Load(uc_1_load),
    .R_W(uc_1_r_w));
  Clock clock_1 (.out(clock_1_out));
  Button Reset (.out(Reset_out));
  ROM #(.addrWidth(4)) rom_1 (.addr(counter_1_q), .data(rom_1_data));  // open: sel
  IR ir_1 (.D(rom_1_data), .Clock(uc_1_clk_ri), .Q(ir_1_q));
  // Probe on flipflop_1_q
  Mux mux_1 (.E(uc_1_operando), .Controle(uc_1_e), .D(ram_1_data), .out_4(mux_1_out_4));
  // Probe on mux_1_out_4
  ULA ula_1 (
    .D(\uc_1_direção ), .A(flipflop_1_q), .B(mux_1_out_4), .Overflow(ula_1_overflow),
    .\Operações (\uc_1_operação ), .S(ula_1_s), .Zero(ula_1_zero));
  // Probe on ula_1_s
  FlipFlop flipflop_1 (.D(ula_1_s), .Q(flipflop_1_q), .in_1(uc_1_clk_ac));
  D_Flip_Flop d_ff_1 (.clk(uc_1_clk_ac), .D(ula_1_overflow), .Q(d_ff_1_q));  // open: Qn, preset, en, reset
  D_Flip_Flop d_ff_2 (.clk(uc_1_clk_ac), .D(ula_1_zero), .Q(d_ff_2_q));  // open: Qn, preset, en, reset
  RAM #(.addrWidth(4), .dataWidth(4)) ram_1 (
    .addr(\uc_1_b_endereço ), .data(ram_1_data), .clk(uc_1_clk_ram), .ld(uc_1_r_w));  // open: sel, clr
  not not_2 (not_2_out, uc_1_r_w);
  BUFFER buffer_1 (.in_1(flipflop_1_q), .in_2(not_2_out), .out_3(ram_1_data));

  // Notes on the sheet:
  //   MOV
  //   0
  //   1
  //   MOV
  //   2
  //   ADD
  //   3
  //   ADD
  //   SUB
  //   4
  //   5
  //   SUB
  //   6
  //   OR
  //   7
  //   OR
  //   8
  //   NOT
  //   NOT
  //   9
  //   A
  //   SHF
  //   SHF
  //   B
  //   JPZ
  //   C
  //   JPO
  //   D
  //   GO
  //   E
  //   STR
  //   F
  //   Instruction Set
  //   0
  //   000
  //   AC <= X
  //   1
  //   AC <= M(X)
  //   000
  //   0
  //   AC <= AC+X
  //   001
  //   1
  //   001
  //   AC <= AC+M(X)
  //   0
  //   010
  //   AC <= AC-X
  //   010
  //   1
  //   AC <= AC-M(X)
  //   0
  //   011
  //   1
  //   011
  //   0
  //   100
  //   AC <= NOT X
  //   100
  //   1
  //   0
  //   101
  //   AC <= AC << Q
  //   1
  //   101
  //   AC <= AC >> Q
  //   0
  //   110
  //   1
  //   110
  //   PC <= X
  //   0
  //   111
  //   M(X) <= AC 
  //   1
  //   111
  //   AC <= AC OR X
  //   AC <= AC OR M(X)
  //   AC <= NOT M( X)
  //   PC <= X SE FLAG Z
  //   PC <= X SE FLAG O
  //   contents of rom_1 (hex, n*v repeats v):
  //   0 f0 1 f1 10 31 d0 f2 11 f0 12 f1 e4
endmodule

module ADD_1 (
  input  A,
  input  B,
  input  VEM_1,
  output S,
  output VAL_1
);

  wire and_1_out, and_2_out, or_1_out, xor_1_out;

  xor xor_1 (xor_1_out, A, B);
  or or_1 (or_1_out, B, VEM_1);
  and and_1 (and_1_out, or_1_out, A);
  and and_2 (and_2_out, B, VEM_1);
  xor xor_2 (S, xor_1_out, VEM_1);
  or or_2 (VAL_1, and_1_out, and_2_out);
endmodule

module SUB_1 (
  input  A,
  input  B,
  input  VEM_1,
  output S,
  output VAI_1
);

  wire and_1_out, and_2_out, not_1_out, or_1_out, xor_1_out;

  not not_1 (not_1_out, A);
  xor xor_1 (xor_1_out, A, B);
  or or_1 (or_1_out, VEM_1, B);
  and and_1 (and_1_out, or_1_out, not_1_out);
  and and_2 (and_2_out, B, VEM_1);
  xor xor_2 (S, xor_1_out, VEM_1);
  or or_2 (VAI_1, and_1_out, and_2_out);
endmodule

module ADD_4 (
  input  [3:0] in_1,
  input  [3:0] in_2,
  input  in_3,
  output out_4,
  output [3:0] out_5
);

  wire add_1_2_val_1, add_1_3_val_1, add_1_4_val_1;

  ADD_1 add_1_1 (.A(in_1[3]), .B(in_2[3]), .VEM_1(add_1_2_val_1), .S(out_5[3]), .VAL_1(out_4));
  ADD_1 add_1_2 (.A(in_1[2]), .B(in_2[2]), .VEM_1(add_1_3_val_1), .S(out_5[2]), .VAL_1(add_1_2_val_1));
  ADD_1 add_1_3 (.A(in_1[1]), .B(in_2[1]), .VEM_1(add_1_4_val_1), .S(out_5[1]), .VAL_1(add_1_3_val_1));
  ADD_1 add_1_4 (.A(in_1[0]), .B(in_2[0]), .VEM_1(in_3), .S(out_5[0]), .VAL_1(add_1_4_val_1));

  // Notes on the sheet:
  //   ADD_1
  //   ADD_1
  //   ADD_1
endmodule

module SUB_4 (
  input  [3:0] in_1,
  input  [3:0] in_2,
  input  in_3,
  output out_4,
  output [3:0] out_5
);

  wire sub_1_2_vai_1, sub_1_3_vai_1, sub_1_4_vai_1;

  SUB_1 sub_1_1 (.A(in_2[3]), .B(in_1[3]), .VEM_1(sub_1_2_vai_1), .S(out_5[3]), .VAI_1(out_4));
  SUB_1 sub_1_2 (.A(in_2[2]), .B(in_1[2]), .VEM_1(sub_1_3_vai_1), .S(out_5[2]), .VAI_1(sub_1_2_vai_1));
  SUB_1 sub_1_3 (.A(in_2[1]), .B(in_1[1]), .VEM_1(sub_1_4_vai_1), .S(out_5[1]), .VAI_1(sub_1_3_vai_1));
  SUB_1 sub_1_4 (.A(in_2[0]), .B(in_1[0]), .VEM_1(in_3), .S(out_5[0]), .VAI_1(sub_1_4_vai_1));
endmodule

module BUFFER (
  input  [3:0] in_1,
  input  in_2,
  output [3:0] out_3
);

  assign out_3[3] = in_2 ? in_1[3] : 1'bz;  // Controlled_Buffer controlled_buffer_1
  assign out_3[0] = in_2 ? in_1[0] : 1'bz;  // Controlled_Buffer controlled_buffer_2
  assign out_3[2] = in_2 ? in_1[2] : 1'bz;  // Controlled_Buffer controlled_buffer_3
  assign out_3[1] = in_2 ? in_1[1] : 1'bz;  // Controlled_Buffer controlled_buffer_4
endmodule

module BUFFER_INVERTIDO (
  input  [3:0] in_1,
  input  in_2,
  output [3:0] out_3
);

  assign out_3[3] = in_2 ? ~in_1[3] : 1'bz;  // Controlled_Inverter controlled_inverter_1
  assign out_3[2] = in_2 ? ~in_1[2] : 1'bz;  // Controlled_Inverter controlled_inverter_2
  assign out_3[1] = in_2 ? ~in_1[1] : 1'bz;  // Controlled_Inverter controlled_inverter_3
  assign out_3[0] = in_2 ? ~in_1[0] : 1'bz;  // Controlled_Inverter controlled_inverter_4
endmodule

module DECODER (
  input  [2:0] \OPERAÇÃO ,
  output S0,
  output S1,
  output S2,
  output S3,
  output S4,
  output S5,
  output S6,
  output S7
);

  wire not_1_out, not_2_out, not_3_out, not_4_out, not_5_out, not_6_out, not_7_out, not_8_out, not_9_out,
       not_10_out, not_11_out, not_12_out;

  not not_1 (not_1_out, \OPERAÇÃO [2]);
  not not_2 (not_2_out, \OPERAÇÃO [1]);
  and and_1 (S0, not_1_out, not_2_out, not_3_out);
  not not_3 (not_3_out, \OPERAÇÃO [0]);
  not not_4 (not_4_out, \OPERAÇÃO [2]);
  and and_2 (S1, not_4_out, not_5_out, \OPERAÇÃO [0]);
  not not_5 (not_5_out, \OPERAÇÃO [1]);
  not not_6 (not_6_out, \OPERAÇÃO [2]);
  and and_3 (S2, not_6_out, \OPERAÇÃO [1], not_7_out);
  not not_7 (not_7_out, \OPERAÇÃO [0]);
  not not_8 (not_8_out, \OPERAÇÃO [2]);
  and and_4 (S3, not_8_out, \OPERAÇÃO [1], \OPERAÇÃO [0]);
  not not_9 (not_9_out, \OPERAÇÃO [1]);
  and and_5 (S4, \OPERAÇÃO [2], not_9_out, not_10_out);
  not not_10 (not_10_out, \OPERAÇÃO [0]);
  and and_6 (S5, \OPERAÇÃO [2], not_11_out, \OPERAÇÃO [0]);
  not not_11 (not_11_out, \OPERAÇÃO [1]);
  and and_7 (S6, \OPERAÇÃO [2], \OPERAÇÃO [1], not_12_out);
  not not_12 (not_12_out, \OPERAÇÃO [0]);
  and and_8 (S7, \OPERAÇÃO [2], \OPERAÇÃO [1], \OPERAÇÃO [0]);
endmodule

module ROT_L (
  input  [3:0] ABCD,
  input  [1:0] XY,
  output [3:0] abcd_2
);

  wire and_1_out, and_2_out, and_3_out, and_4_out, and_5_out, and_6_out, and_7_out, and_8_out, and_9_out;

  and and_1 (and_1_out, ~XY[1], ~XY[0], ABCD[3]);  // AND_Gate
  and and_2 (and_2_out, ~XY[1], XY[0], ABCD[2]);  // AND_Gate
  or or_1 (abcd_2[3], and_1_out, and_2_out, and_3_out, and_4_out);
  and and_3 (and_3_out, XY[1], ~XY[0], ABCD[1]);  // AND_Gate
  and and_4 (and_4_out, XY[1], XY[0], ABCD[0]);
  and and_5 (and_5_out, ~XY[1], ~XY[0], ABCD[2]);  // AND_Gate
  or or_2 (abcd_2[2], and_5_out, and_6_out, and_7_out);
  and and_6 (and_6_out, ~XY[1], XY[0], ABCD[1]);  // AND_Gate
  and and_7 (and_7_out, XY[1], ~XY[0], ABCD[0]);  // AND_Gate
  and and_8 (and_8_out, ~XY[1], ~XY[0], ABCD[1]);  // AND_Gate
  or or_3 (abcd_2[1], and_8_out, and_9_out);
  and and_9 (and_9_out, ~XY[1], XY[0], ABCD[0]);  // AND_Gate
  and and_10 (abcd_2[0], ~XY[1], ~XY[0], ABCD[0]);  // AND_Gate
endmodule

module ROT_R (
  input  [3:0] ABCD,
  input  [1:0] XY,
  output [3:0] abcd_2
);

  wire and_1_out, and_2_out, and_3_out, and_4_out, and_5_out, and_6_out, and_7_out, and_8_out, and_9_out;

  and and_1 (and_1_out, ~XY[1], ~XY[0], ABCD[0]);  // AND_Gate
  and and_2 (and_2_out, ~XY[1], XY[0], ABCD[1]);  // AND_Gate
  or or_1 (abcd_2[0], and_1_out, and_2_out, and_3_out, and_4_out);
  and and_3 (and_3_out, XY[1], ~XY[0], ABCD[2]);  // AND_Gate
  and and_4 (and_4_out, XY[1], XY[0], ABCD[3]);
  and and_5 (and_5_out, ~XY[1], ~XY[0], ABCD[1]);  // AND_Gate
  and and_6 (and_6_out, ~XY[1], XY[0], ABCD[2]);  // AND_Gate
  or or_2 (abcd_2[1], and_5_out, and_6_out, and_7_out);
  and and_7 (and_7_out, XY[1], ~XY[0], ABCD[3]);  // AND_Gate
  and and_8 (and_8_out, ~XY[1], ~XY[0], ABCD[2]);  // AND_Gate
  or or_3 (abcd_2[2], and_8_out, and_9_out);
  and and_9 (and_9_out, ~XY[1], XY[0], ABCD[3]);  // AND_Gate
  and and_10 (abcd_2[3], ~XY[1], ~XY[0], ABCD[3]);  // AND_Gate
endmodule

module OR_4 (
  input  [3:0] A,
  input  [3:0] B,
  output [3:0] S
);

  or or_1 (S[3], A[3], B[3]);
  or or_2 (S[2], A[2], B[2]);
  or or_3 (S[1], A[1], B[1]);
  or or_4 (S[0], A[0], B[0]);
endmodule

module ULA (
  input  D,
  input  [3:0] A,
  input  [3:0] B,
  input  [2:0] \Operações ,
  output Overflow,
  output [3:0] S,
  output Zero
);

  wire add_4_1_out_4, and_1_out, and_2_out, decoder_1_s0, decoder_1_s1, decoder_1_s2, decoder_1_s3,
       decoder_1_s4, decoder_1_s5, decoder_1_s6, decoder_1_s7, not_1_out, sub_4_1_out_4;
  wire [3:0] add_4_1_out_5, buffer_5_out_3, or_4_1_s, rot_l_1_abcd_2, rot_r_1_abcd_2, sub_4_1_out_5;

  or or_1 (Overflow, and_1_out, and_2_out);
  and and_1 (and_1_out, add_4_1_out_4, decoder_1_s1);
  and and_2 (and_2_out, sub_4_1_out_4, decoder_1_s2);
  DECODER decoder_1 (
    .\OPERAÇÃO (\Operações ), .S0(decoder_1_s0), .S1(decoder_1_s1), .S2(decoder_1_s2), .S3(decoder_1_s3),
    .S4(decoder_1_s4), .S5(decoder_1_s5), .S6(decoder_1_s6), .S7(decoder_1_s7));
  BUFFER buffer_1 (.in_1(B), .in_2(decoder_1_s0), .out_3(S));
  nor nor_1 (Zero, decoder_1_s7, decoder_1_s6, S[0], S[1], S[2], S[3]);
  ADD_4 add_4_1 (.in_1(A), .in_2(B), .out_4(add_4_1_out_4), .in_3(1'b0), .out_5(add_4_1_out_5));
  BUFFER buffer_2 (.in_1(add_4_1_out_5), .in_2(decoder_1_s1), .out_3(S));
  // Probe on A
  // Probe on B
  SUB_4 sub_4_1 (.in_2(A), .out_4(sub_4_1_out_4), .in_1(B), .in_3(1'b0), .out_5(sub_4_1_out_5));
  BUFFER buffer_3 (.in_1(sub_4_1_out_5), .in_2(decoder_1_s2), .out_3(S));
  OR_4 or_4_1 (.A(A), .B(B), .S(or_4_1_s));
  BUFFER buffer_4 (.in_1(or_4_1_s), .in_2(decoder_1_s3), .out_3(S));
  // Probe on S
  BUFFER_INVERTIDO buffer_invertido_1 (.in_1(B), .in_2(decoder_1_s4), .out_3(S));
  ROT_R rot_r_1 (.abcd_2(rot_r_1_abcd_2), .ABCD(A), .XY(B[1:0]));
  ROT_L rot_l_1 (.abcd_2(rot_l_1_abcd_2), .ABCD(A), .XY(B[1:0]));
  BUFFER buffer_5 (.in_1(rot_r_1_abcd_2), .in_2(D), .out_3(buffer_5_out_3));
  BUFFER buffer_6 (.in_1(rot_l_1_abcd_2), .in_2(not_1_out), .out_3(buffer_5_out_3));
  not not_1 (not_1_out, D);
  BUFFER buffer_7 (.in_1(buffer_5_out_3), .in_2(decoder_1_s5), .out_3(S));
endmodule

module FlipFlop (
  input  in_1,
  input  [3:0] D,
  output [3:0] Q
);

  D_Flip_Flop D3 (.clk(in_1), .D(D[3]), .Q(Q[3]));  // open: Qn, preset, en, reset
  D_Flip_Flop D2 (.clk(in_1), .D(D[2]), .Q(Q[2]));  // open: Qn, preset, en, reset
  D_Flip_Flop D1 (.clk(in_1), .D(D[1]), .Q(Q[1]));  // open: Qn, preset, en, reset
  D_Flip_Flop D0 (.clk(in_1), .D(D[0]), .Q(Q[0]));  // open: Qn, preset, en, reset
endmodule

module Mux (
  input  [3:0] E,
  input  [3:0] D,
  input  Controle,
  output [3:0] out_4
);

  wire not_1_out;

  not not_1 (not_1_out, Controle);
  BUFFER buffer_1 (.in_1(E), .in_2(not_1_out), .out_3(out_4));
  BUFFER buffer_2 (.in_1(D), .in_2(Controle), .out_3(out_4));
endmodule

module IR (
  input  Clock,
  input  [7:0] D,
  output [7:0] Q
);

  D_Flip_Flop #(.trigger("falling")) D3 (.clk(Clock), .D(D[7]), .Q(Q[7]));  // open: Qn, preset, en, reset
  D_Flip_Flop #(.trigger("falling")) D2 (.clk(Clock), .D(D[6]), .Q(Q[6]));  // open: Qn, preset, en, reset
  D_Flip_Flop #(.trigger("falling")) D1 (.clk(Clock), .D(D[5]), .Q(Q[5]));  // open: Qn, preset, en, reset
  D_Flip_Flop #(.trigger("falling")) D0 (.clk(Clock), .D(D[4]), .Q(Q[4]));  // open: Qn, preset, en, reset
  D_Flip_Flop #(.trigger("falling")) D3_2 (.clk(Clock), .D(D[3]), .Q(Q[3]));  // open: Qn, preset, en, reset
  D_Flip_Flop #(.trigger("falling")) D2_2 (.clk(Clock), .D(D[2]), .Q(Q[2]));  // open: Qn, preset, en, reset
  D_Flip_Flop #(.trigger("falling")) D1_2 (.clk(Clock), .D(D[1]), .Q(Q[1]));  // open: Qn, preset, en, reset
  D_Flip_Flop #(.trigger("falling")) D1_3 (.clk(Clock), .D(D[0]), .Q(Q[0]));  // open: Qn, preset, en, reset
endmodule

module UC (
  input  [7:0] \Instrução ,
  input  Clock,
  input  Reset,
  input  Overflow,
  input  Zero,
  output [3:0] Dados,
  output [3:0] \B_ENDEREÇO ,
  output Rst_PC,
  output clk_RI,
  output clk_PC,
  output clk_AC,
  output clk_RAM,
  output [3:0] Operando,
  output \Direção ,
  output E,
  output [2:0] \Operação ,
  output R_W,
  output Load
);

  wire GoTo_out, JPO_out, JPZ_out, nand_1_out;
  wire [1:0] counter_1_q;

  nand Storage (R_W, \Instrução [7], \Instrução [6], \Instrução [5], \Instrução [4], clk_AC);
  and GoTo (GoTo_out, \Instrução [7], \Instrução [6], \Instrução [5], ~\Instrução [4], clk_PC);  // AND_Gate
  Counter #(.width(2), .max('h3)) counter_1 (.Q(counter_1_q), .clk(Clock), .clr(Reset));  // open: load, D, count, carry
  and and_1 (clk_RI, ~counter_1_q[0], ~counter_1_q[0]);  // AND_Gate
  and JPO (JPO_out, \Instrução [7], \Instrução [6], ~\Instrução [5], \Instrução [4], clk_PC, Overflow);  // AND_Gate
  or or_1 (Load, GoTo_out, JPO_out, JPZ_out);
  and and_2 (clk_PC, counter_1_q[0], ~counter_1_q[1]);  // AND_Gate
  and and_3 (clk_AC, ~counter_1_q[0], counter_1_q[1]);  // AND_Gate
  and JPZ (JPZ_out, \Instrução [7], \Instrução [6], ~\Instrução [5], ~\Instrução [4], clk_PC, Zero);  // AND_Gate
  and and_4 (clk_RAM, counter_1_q[0], counter_1_q[1]);
  and and_5 (E, \Instrução [4], nand_1_out);
  nand nand_1 (nand_1_out, \Instrução [7], ~\Instrução [6], \Instrução [5]);  // NAND_Gate

  assign \B_ENDEREÇO  = \Instrução [3:0];
  assign Dados = \Instrução [3:0];
  assign \Direção  = \Instrução [4];
  assign Operando = \Instrução [3:0];
  assign \Operação  = \Instrução [7:5];
  assign Rst_PC = Reset;
endmodule
